// Logisim project cpu.circ as structural Verilog: 5 circuits, main circuit main
module main (
  input  [31:0] INSTRUCTION,
  input  CLOCK,
  output [31:0] FETCH_ADDRESS,
  output [31:0] s0_Value,
  output [31:0] s1_Value,
  output [31:0] s2_Value,
  output [31:0] ra_Value,
  output [31:0] sp_Value
);

  wire ALUSrc, equal, equal_ctrl, ExtOp, ifBranch, Jump, JumpR, Lui, main_2_signed_overflow, MemtoReg,
       MemWrite, not_1_out, NotEq, nPCsel, or_1_out, RegWrite, Shift;
  wire [1:0] RegDst;
  wire [3:0] ALUctr;
  wire [4:0] multiplexer_6_out;
  wire [25:0] addr;
  wire [31:0] ALU_out, bit_extender_1_out, BranchAddr, Extender_2_extended_number,
       extender_3_extended_number, Extender_extended_number, fetch_in, luiImm, multiplexer_1_out,
       multiplexer_2_out, multiplexer_7_out, multiplexer_8_out, multiplexer_9_out, multiplexer_10_out,
       multiplexer_11_out, multiplier_1_out, PC_4, PC_input, RAM_out, Reg_out1, Reg_out2;
  wire [31:26] fetch_out;

  Multiplexer #(.width(32)) multiplexer_1 (
    .in0(PC_4), .in1(BranchAddr), .out(multiplexer_1_out), .sel(ifBranch));  // open: en
  // mem_main main_1: pin names not known; wires that end beside it: ALU_out, Reg_out2, MemWrite, CLOCK, RAM_out
  Register #(.width(32)) Fetch_Register (.D(fetch_in), .Q({fetch_out, addr}), .clk(CLOCK));  // open: en, clr
  Register #(.width(32)) PC (.D(PC_input), .Q(FETCH_ADDRESS), .clk(CLOCK));  // open: en, clr
  and and_1 (ifBranch, nPCsel, equal_ctrl);
  Extender Extender (.Immediate(addr[15:0]), .Signed(1'b1), .Extended_Number(Extender_extended_number));
  Multiplexer #(.width(32)) multiplexer_2 (
    .in0(multiplexer_1_out), .in1(Reg_out1), .out(multiplexer_2_out), .sel(JumpR));  // open: en
  or or_1 (or_1_out, ifBranch, Jump);
  not not_1 (not_1_out, equal);
  Multiplier #(.width(32)) multiplier_1 (
    .a(Extender_extended_number), .b(32'h4), .out(multiplier_1_out));  // open: cin, cout
  // Probe on addr[5:0]
  // Probe on addr[10:6]
  // Probe on addr[15:11]
  // Probe on addr[20:16]
  // Probe on addr[25:21]
  // Probe on fetch_out
  // Probe on addr[15:0]
  // Probe on addr
  // Probe on BranchAddr
  // Probe on {FETCH_ADDRESS[31:28], addr, 2'b00}
  // Probe on PC_input
  // Probe on FETCH_ADDRESS
  // Probe on PC_4
  // Probe on RegDst
  // Probe on ALUctr
  // Probe on Reg_out1
  // Probe on Reg_out2
  // Probe on RAM_out
  // Probe on ALU_out
  Multiplexer #(.width(32)) multiplexer_3 (
    .in0(INSTRUCTION), .in1({32{1'b0}}), .out(fetch_in), .sel(or_1_out));  // open: en
  Adder #(.width(32)) adder_1 (.a(FETCH_ADDRESS), .b(32'h4), .out(PC_4));  // open: cin, cout
  Multiplexer multiplexer_4 (.in0(equal), .in1(not_1_out), .out(equal_ctrl), .sel(NotEq));  // open: en
  Adder #(.width(32)) adder_2 (.a(multiplier_1_out), .b(FETCH_ADDRESS), .out(BranchAddr));  // open: cin, cout
  Multiplexer #(.width(32)) multiplexer_5 (
    .in0(multiplexer_2_out), .in1({FETCH_ADDRESS[31:28], addr, 2'b00}), .out(PC_input), .sel(Jump));  // open: en
  assign bit_extender_1_out = {{27{1'b0}}, addr[10:6]};  // Bit_Extender bit_extender_1
  Multiplexer #(.select(2), .width(5)) multiplexer_6 (
    .in0(addr[20:16]), .in1(addr[15:11]), .in2({5{1'b1}}), .in3(addr[25:21]), .out(multiplexer_6_out),
    .sel(RegDst));  // open: en
  Extender Extender_2 (.Immediate(addr[15:0]), .Signed(1'b0), .Extended_Number(Extender_2_extended_number));
  Control control_1 (
    .Funct(addr[5:0]), .Opcode(fetch_out), .JumpR(JumpR), .NotEq(NotEq), .RegDst(RegDst), .ALUSrc(ALUSrc),
    .MemtoReg(MemtoReg), .RegWrite(RegWrite), .MemWrite(MemWrite), .nPCsel(nPCsel), .Jump(Jump),
    .ExtOp(ExtOp), .ALUctr(ALUctr), .Shift(Shift), .Lui(Lui));
  Multiplexer #(.width(32)) multiplexer_7 (
    .in0(Reg_out1), .in1(bit_extender_1_out), .out(multiplexer_7_out), .sel(Shift));  // open: en
  Extender extender_3 (.Immediate(addr[15:0]), .Signed(ExtOp), .Extended_Number(extender_3_extended_number));
  Multiplexer #(.width(32)) multiplexer_8 (
    .in0(multiplexer_9_out), .in1(RAM_out), .out(multiplexer_8_out), .sel(MemtoReg));  // open: en
  Multiplexer #(.width(32)) multiplexer_9 (
    .in0(multiplexer_10_out), .in1(FETCH_ADDRESS), .out(multiplexer_9_out), .sel(Jump));  // open: en
  Multiplexer #(.width(32)) multiplexer_10 (
    .in0(ALU_out), .in1(luiImm), .out(multiplexer_10_out), .sel(Lui));  // open: en
  Shifter #(.width(32)) shifter_1 (.in(Extender_2_extended_number), .\dist (5'b10000), .out(luiImm));
  LED led_1 (.in(main_2_signed_overflow));
  alu_main main_2 (
    .Switch(ALUctr), .X(multiplexer_7_out), .Equal(equal), .Result(ALU_out),
    .Signed_Overflow(main_2_signed_overflow), .Y(multiplexer_11_out));
  Multiplexer #(.width(32)) multiplexer_11 (
    .in0(Reg_out2), .in1(extender_3_extended_number), .out(multiplexer_11_out), .sel(ALUSrc));  // open: en
  regfile_main main_3 (
    .Read_Register_1(addr[25:21]), .Read_Register_2(addr[20:16]), .Write_Register(multiplexer_6_out),
    .Write_Data(multiplexer_8_out), .Write_Enable(RegWrite), .Clock(CLOCK), .Read_Data_1(Reg_out1),
    .Read_Data_2(Reg_out2), .s0_Value(s0_Value), .s1_Value(s1_Value), .s2_Value(s2_Value),
    .ra_Value(ra_Value), .sp_Value(sp_Value));

  // Other names for the same wires on the sheet: clk = CLOCK; fetch_addr[31:0] = FETCH_ADDRESS;
  //   opcode[5:0] = fetch_out; fetch_out[25:0] = addr; funct[5:0] = addr[5:0]; imm[15:0] = addr[15:0];
  //   JumpAddr[31:2] = {FETCH_ADDRESS[31:28], addr}; shamt[4:0] = addr[10:6]; rd[4:0] = addr[15:11];
  //   rt[4:0] = addr[20:16]; rs[4:0] = addr[25:21]; ra[31:0] = ra_Value; s0[31:0] = s0_Value; s1[31:0] = s1_Value;
  //   s2[31:0] = s2_Value; sp[31:0] = sp_Value

  // Notes on the sheet:
  //   Output
  //   These are outputs/inputs from run.circ
  //   Inputs
  //   These are DEBUG/TEST outputs from your circuit.
endmodule

module Extender (
  input  [15:0] Immediate,
  input  Signed,
  output [31:0] Extended_Number
);

  wire [31:0] bit_extender_1_out, bit_extender_2_out;

  assign bit_extender_1_out = {{16{1'b0}}, Immediate};  // Bit_Extender bit_extender_1
  assign bit_extender_2_out = {{16{Immediate[15]}}, Immediate};  // Bit_Extender bit_extender_2
  Multiplexer #(.width(32)) multiplexer_1 (
    .in0(bit_extender_1_out), .in1(bit_extender_2_out), .out(Extended_Number), .sel(Signed));  // open: en
endmodule

module Translator (
  input  [5:0] Funct,
  input  [5:0] Opcode,
  output add,
  output addu,
  output \and ,
  output jr,
  output \or ,
  output slt,
  output sltu,
  output sll,
  output sra,
  output srl,
  output sub,
  output subu,
  output addi,
  output addiu,
  output andi,
  output beq,
  output bne,
  output lui,
  output lw,
  output ori,
  output slti,
  output sltiu,
  output sw,
  output swinc,
  output j,
  output jal
);

  wire f_0, f_0x0, f_0x1, f_0x2, f_0x3, f_1, f_2, f_3, f_4, f_5, f_6, f_7, f_8, f_9, f_a, f_b, f_c, f_d, f_e,
       f_f, itype, jtype, o_0, o_0x0, o_0x1, o_0x2, o_0x3, o_1, o_2, o_3, o_4, o_5, o_6, o_7, o_8, o_9, o_a,
       o_b, o_c, o_d, o_e, o_f, rtype;

  Decoder #(.select(4), .enable("false")) decoder_1 (
    .out0(f_0), .out1(f_1), .out2(f_2), .out3(f_3), .out4(f_4), .out5(f_5), .out6(f_6), .out7(f_7),
    .out8(f_8), .out9(f_9), .out10(f_a), .out11(f_b), .out12(f_c), .out13(f_d), .out14(f_e), .out15(f_f),
    .sel(Funct[3:0]));
  Decoder #(.select(4), .enable("false")) decoder_2 (
    .out0(o_0), .out1(o_1), .out2(o_2), .out3(o_3), .out4(o_4), .out5(o_5), .out6(o_6), .out7(o_7),
    .out8(o_8), .out9(o_9), .out10(o_a), .out11(o_b), .out12(o_c), .out13(o_d), .out14(o_e), .out15(o_f),
    .sel(Opcode[3:0]));
  Decoder #(.select(2), .enable("false")) decoder_3 (
    .out0(f_0x0), .out1(f_0x1), .out2(f_0x2), .out3(f_0x3), .sel(Funct[5:4]));
  Decoder #(.select(2), .enable("false")) decoder_4 (
    .out0(o_0x0), .out1(o_0x1), .out2(o_0x2), .out3(o_0x3), .sel(Opcode[5:4]));
  Type_Checker type_checker_1 (.Opcode(Opcode), .rtype(rtype), .itype(itype), .jtype(jtype));
  and and_1 (add, f_0x2, f_0, rtype);
  and and_2 (addu, f_0x2, f_1, rtype);
  and and_3 (\and , f_0x2, f_4, rtype);
  and and_4 (jr, f_0x0, f_8, rtype);
  and and_5 (\or , f_0x2, f_5, rtype);
  and and_6 (slt, f_0x2, f_a, rtype);
  and and_7 (sltu, f_0x2, f_b, rtype);
  and and_8 (sll, f_0x0, f_0, rtype);
  and and_9 (sra, f_0x0, f_3, rtype);
  and and_10 (srl, f_0x0, f_2, rtype);
  and and_11 (sub, f_0x2, f_2, rtype);
  and and_12 (subu, f_0x2, f_3, rtype);
  and and_13 (addi, o_0x0, o_8, itype);
  and and_14 (addiu, o_0x0, o_9, itype);
  and and_15 (andi, o_0x0, o_c, itype);
  and and_16 (beq, o_0x0, o_4, itype);
  and and_17 (bne, o_0x0, o_5, itype);
  and and_18 (lui, o_0x0, o_f, itype);
  and and_19 (lw, o_0x2, o_3, itype);
  and and_20 (ori, o_0x0, o_d, itype);
  and and_21 (slti, o_0x0, o_a, itype);
  and and_22 (sltiu, o_0x0, o_b, itype);
  and and_23 (sw, o_0x2, o_b, itype);
  and and_24 (swinc, o_0x2, o_c, itype);
  and and_25 (j, o_0x0, o_2, jtype);
  and and_26 (jal, o_0x0, o_3, jtype);
endmodule

// Type
module Type_Checker (
  input  [5:0] Opcode,
  output rtype,
  output itype,
  output jtype
);

  wire comparator_2_lt, not_1_out, not_2_out;

  Comparator #(.width(6), .mode("unsigned")) comparator_1 (.a({6{1'b0}}), .b(Opcode), .eq(rtype));  // open: gt, lt
  not not_1 (not_1_out, rtype);
  Comparator #(.width(6), .mode("unsigned")) comparator_2 (
    .a(Opcode), .b(6'b000100), .lt(comparator_2_lt));  // open: gt, eq
  not not_2 (not_2_out, comparator_2_lt);
  and and_1 (itype, not_1_out, not_2_out);
  and and_2 (jtype, not_1_out, comparator_2_lt);
endmodule

module Control (
  input  [5:0] Funct,
  input  [5:0] Opcode,
  output JumpR,
  output NotEq,
  output [1:0] RegDst,
  output ALUSrc,
  output MemtoReg,
  output RegWrite,
  output MemWrite,
  output nPCsel,
  output Jump,
  output ExtOp,
  output [3:0] ALUctr,
  output Shift,
  output Lui
);

  wire add, addi, addiu, addu, \and , andi, beq, itype, j, jal, jtype, \or , ori, rtype, sll, slt, slti,
       sltiu, sltu, sra, srl, sub, subu, sw, swinc;

  Type_Checker type_checker_1 (.Opcode(Opcode), .rtype(rtype), .itype(itype), .jtype(jtype));
  or or_1 (MemWrite, sw, swinc);
  or or_2 (nPCsel, beq, NotEq);
  or or_3 (Jump, j, jal);
  Translator translator_1 (
    .Funct(Funct), .Opcode(Opcode), .add(add), .addu(addu), .\and (\and ), .jr(JumpR), .\or (\or ),
    .slt(slt), .sltu(sltu), .sll(sll), .sra(sra), .srl(srl), .sub(sub), .subu(subu), .addi(addi),
    .addiu(addiu), .andi(andi), .beq(beq), .bne(NotEq), .lui(Lui), .lw(MemtoReg), .ori(ori), .slti(slti),
    .sltiu(sltiu), .sw(sw), .swinc(swinc), .j(j), .jal(jal));
  or or_4 (ALUSrc, sw, MemtoReg, addi, addiu, andi, ori, slti, sltiu, Lui, swinc);
  or or_5 (Shift, sll, sra, srl);
  nor nor_1 (RegWrite, nPCsel, j, JumpR, sw);
  or or_6 (ExtOp, addiu, addi, MemtoReg, slti, sltiu, sw, swinc);
  or or_7 (RegDst[0], rtype, swinc);
  or or_8 (RegDst[1], swinc, jal);
  or or_9 (ALUctr[0], addi, andi, add, \and , slt, srl, sub, slti);
  or or_10 (ALUctr[1], sw, swinc, MemtoReg, addiu, addu, \or , slt, sra, sub, ori, slti);
  or or_11 (ALUctr[2], addi, addiu, MemtoReg, add, addu, sltu, sub, sltiu, sw, swinc);
  or or_12 (ALUctr[3], andi, ori, \and , \or , slt, sltu, subu, slti, sltiu);

  // Other names for the same wires on the sheet: bne = NotEq; jr = JumpR; lw = MemtoReg
endmodule
