// Logisim project alu.circ as structural Verilog: 1 circuit, main circuit main
module main (
  input  [31:0] X,
  input  [31:0] Y,
  input  [3:0] Switch,
  input  [30:0] in_4,
  input  [30:0] in_5,
  output Signed_Overflow,
  output Equal,
  output [31:0] Result
);

  wire overflow_5_add, overflow_7_sub, xor_1_out, xor_2_out, xor_3_out, xor_4_out;
  wire [0:0] result_11_slt, result_12_sltu;
  wire [31:0] adder_3_out, negator_1_out, result_0_sll, result_1_srl, result_2_sra, result_5_add,
       result_6_addu, result_7_sub, result_8_subu, result_9_and, result_10_or, x_0_sll, x_1_srl, x_2_sra,
       x_5_add, x_6_addu, x_7_sub, x_8_subu, x_9_and, x_10_or, x_11_slt, x_12_sltu, y_0_sll, y_1_srl,
       y_2_sra, y_5_add, y_6_addu, y_7_sub, y_8_subu, y_9_and, y_10_or, y_11_slt, y_12_sltu;

  Shifter #(.width(32)) shifter_1 (.in(y_0_sll), .\dist (x_0_sll[4:0]), .out(result_0_sll));
  Shifter #(.width(32), .shift("lr")) shifter_2 (.in(y_1_srl), .\dist (x_1_srl[4:0]), .out(result_1_srl));
  Shifter #(.width(32), .shift("ar")) shifter_3 (.in(y_2_sra), .\dist (x_2_sra[4:0]), .out(result_2_sra));
  Adder #(.width(32)) adder_1 (.a(x_5_add), .b(y_5_add), .out(result_5_add));  // open: cin, cout
  Adder #(.width(32)) adder_2 (.a(x_6_addu), .b(y_6_addu), .out(result_6_addu));  // open: cin, cout
  Subtractor #(.width(32)) subtractor_1 (.a(x_7_sub), .b(y_7_sub), .out(result_7_sub));  // open: bin, bout
  Subtractor #(.width(32)) subtractor_2 (.a(x_8_subu), .b(y_8_subu), .out(result_8_subu));  // open: bin, bout
  Comparator #(.width(32), .mode("unsigned")) comparator_1 (.a(X), .b(Y), .eq(Equal));  // open: gt, lt
  assign result_9_and = x_9_and & y_9_and;  // AND_Gate and_1, 32 bits wide
  assign result_10_or = x_10_or | y_10_or;  // OR_Gate or_1, 32 bits wide
  Comparator #(.width(32)) comparator_2 (.a(x_11_slt), .b(y_11_slt), .lt(result_11_slt[0]));  // open: gt, eq
  Comparator #(.width(32), .mode("unsigned")) comparator_3 (
    .a(x_12_sltu), .b(y_12_sltu), .lt(result_12_sltu[0]));  // open: gt, eq
  xor xor_1 (xor_1_out, result_5_add[31], x_5_add[31]);
  xor xor_2 (xor_2_out, x_5_add[31], y_5_add[31]);
  Negator #(.width(32)) negator_1 (.in(y_7_sub), .out(negator_1_out));
  Adder #(.width(32)) adder_3 (.a(negator_1_out), .b(32'h1), .out(adder_3_out));  // open: cin, cout
  Multiplexer multiplexer_1 (.in0(xor_1_out), .in1(1'b0), .out(overflow_5_add), .sel(xor_2_out));  // open: en
  xor xor_3 (xor_3_out, result_7_sub[31], x_7_sub[31]);
  xor xor_4 (xor_4_out, x_7_sub[31], adder_3_out[31]);
  Multiplexer multiplexer_2 (.in0(xor_3_out), .in1(1'b0), .out(overflow_7_sub), .sel(xor_4_out));  // open: en
  Demultiplexer #(.select(4), .width(32)) demultiplexer_1 (
    .out0(x_0_sll), .out1(x_1_srl), .out2(x_2_sra), .out5(x_5_add), .out6(x_6_addu), .out7(x_7_sub),
    .out8(x_8_subu), .out9(x_9_and), .out10(x_10_or), .out11(x_11_slt), .out12(x_12_sltu), .in(X),
    .sel(Switch));  // open: out3, out4, out13, out14, out15, en
  Demultiplexer #(.select(4), .width(32)) demultiplexer_2 (
    .out0(y_0_sll), .out1(y_1_srl), .out2(y_2_sra), .out5(y_5_add), .out6(y_6_addu), .out7(y_7_sub),
    .out8(y_8_subu), .out9(y_9_and), .out10(y_10_or), .out11(y_11_slt), .out12(y_12_sltu), .in(Y),
    .sel(Switch));  // open: out3, out4, out13, out14, out15, en
  Multiplexer #(.select(4)) multiplexer_3 (
    .in0(1'b0), .in1(1'b0), .in2(1'b0), .in3(1'b0), .in4(1'b0), .in5(overflow_5_add), .in6(1'b0),
    .in7(overflow_7_sub), .in8(1'b0), .in9(1'b0), .in10(1'b0), .in11(1'b0), .in12(1'b0), .in13(1'b0),
    .in14(1'b0), .in15(1'b0), .out(Signed_Overflow), .sel(Switch));  // open: en
  Multiplexer #(.select(4), .width(32)) multiplexer_4 (
    .in0(result_0_sll), .in1(result_1_srl), .in2(result_2_sra), .in5(result_5_add), .in6(result_6_addu),
    .in7(result_7_sub), .in8(result_8_subu), .in9(result_9_and), .in10(result_10_or),
    .in11({in_4, result_11_slt[0]}), .in12({in_5, result_12_sltu[0]}), .out(Result), .sel(Switch));  // open: in3, in4, in13, in14, in15, en

  // Other names for the same wires on the sheet: overflow = Signed_Overflow; result_11_slt[31:1] = in_4;
  //   result_12_sltu[31:1] = in_5; S[3:0] = Switch

  // Notes on the sheet:
  //   INPUTS to your circuit
  //   DON'T CHANGE THE LOCATIONS OF THE INPUTS AND OUTPUTS!
  //   OUTPUTS from your circuit
endmodule
