// Logisim project regfile.circ as structural Verilog: 1 circuit, main circuit main
module main (
  input  [4:0] Read_Register_1,
  input  [4:0] Read_Register_2,
  input  [4:0] Write_Register,
  input  [31:0] Write_Data,
  input  Write_Enable,
  input  Clock,
  output [31:0] s0_Value,
  output [31:0] s1_Value,
  output [31:0] s2_Value,
  output [31:0] ra_Value,
  output [31:0] sp_Value,
  output [31:0] Read_Data_1,
  output [31:0] Read_Data_2
);

  wire we_01__at, we_02__v0, we_03__v1, we_04__a0, we_05__a1, we_06__a2, we_07__a3, we_08__a4, we_09__t1,
       we_10__t2, we_11__t3, we_12__t4, we_13__t5, we_14__t6, we_15__t7, we_16__s0, we_17__s1, we_18__s2,
       we_19__s3, we_20__s4, we_21__s5, we_22__s6, we_23__s7, we_24__t8, we_25__t9, we_26__k0, we_27__k1,
       we_28__gp, we_29__sp, we_30__fp, we_31__ra;
  wire [31:0] in_01__at, in_02__v0, in_03__v1, in_04__a0, in_05__a1, in_06__a2, in_07__a3, in_08__t0,
       in_09__t1, in_10__t2, in_11__t3, in_12__t4, in_13__t5, in_14__t6, in_15__t7, in_16__s0, in_17__s1,
       in_18__s2, in_19__s3, in_20__s4, in_21__s5, in_22__s6, in_23__s7, in_24__t8, in_25__t9, in_26__k0,
       in_27__k1, in_28__gp, in_29__sp, in_30__fp, in_31__ra, out_01__at, out_02__v0, out_03__v1, out_04__a0,
       out_05__a1, out_06__a2, out_07__a3, out_08__vo, out_09__t1, out_10__t2, out_11__t3, out_12__t4,
       out_13__t5, out_14__t6, out_15__t7, out_19__s3, out_20__s4, out_21__s5, out_22__s6, out_23__s7,
       out_24__t8, out_25__t9, out_26__k0, out_27__k1, out_28__gp, out_30__fp;

  Demultiplexer #(.select(5)) demultiplexer_1 (
    .out1(we_01__at), .out2(we_02__v0), .out3(we_03__v1), .out4(we_04__a0), .out5(we_05__a1),
    .out6(we_06__a2), .out7(we_07__a3), .out8(we_08__a4), .out9(we_09__t1), .out10(we_10__t2),
    .out11(we_11__t3), .out12(we_12__t4), .out13(we_13__t5), .out14(we_14__t6), .out15(we_15__t7),
    .out16(we_16__s0), .out17(we_17__s1), .out18(we_18__s2), .out19(we_19__s3), .out20(we_20__s4),
    .out21(we_21__s5), .out22(we_22__s6), .out23(we_23__s7), .out24(we_24__t8), .out25(we_25__t9),
    .out26(we_26__k0), .out27(we_27__k1), .out28(we_28__gp), .out29(we_29__sp), .out30(we_30__fp),
    .out31(we_31__ra), .in(Write_Enable), .sel(Write_Register));  // open: out0, en
  Register #(.width(32)) _01__at (.D(in_01__at), .en(we_01__at), .Q(out_01__at), .clk(Clock));  // open: clr
  Register #(.width(32)) _02__v0 (.D(in_02__v0), .en(we_02__v0), .Q(out_02__v0), .clk(Clock));  // open: clr
  Register #(.width(32)) _03__v1 (.D(in_03__v1), .en(we_03__v1), .Q(out_03__v1), .clk(Clock));  // open: clr
  Register #(.width(32)) _04__a0 (.D(in_04__a0), .en(we_04__a0), .Q(out_04__a0), .clk(Clock));  // open: clr
  Register #(.width(32)) _05__a1 (.D(in_05__a1), .en(we_05__a1), .Q(out_05__a1), .clk(Clock));  // open: clr
  Register #(.width(32)) _06__a2 (.D(in_06__a2), .en(we_06__a2), .Q(out_06__a2), .clk(Clock));  // open: clr
  Register #(.width(32)) _07__a3 (.D(in_07__a3), .en(we_07__a3), .Q(out_07__a3), .clk(Clock));  // open: clr
  Multiplexer #(.select(5), .width(32)) multiplexer_1 (
    .in0({32{1'b0}}), .in1(out_01__at), .in2(out_02__v0), .in3(out_03__v1), .in4(out_04__a0),
    .in5(out_05__a1), .in6(out_06__a2), .in7(out_07__a3), .in8(out_08__vo), .in9(out_09__t1),
    .in10(out_10__t2), .in11(out_11__t3), .in12(out_12__t4), .in13(out_13__t5), .in14(out_14__t6),
    .in15(out_15__t7), .in16(s0_Value), .in17(s1_Value), .in18(s2_Value), .in19(out_19__s3),
    .in20(out_20__s4), .in21(out_21__s5), .in22(out_22__s6), .in23(out_23__s7), .in24(out_24__t8),
    .in25(out_25__t9), .in26(out_26__k0), .in27(out_27__k1), .in28(out_28__gp), .in29(sp_Value),
    .in30(out_30__fp), .in31(ra_Value), .out(Read_Data_1), .sel(Read_Register_1));  // open: en
  Register #(.width(32)) _08__t0 (.D(in_08__t0), .en(we_08__a4), .Q(out_08__vo), .clk(Clock));  // open: clr
  Register #(.width(32)) _09__t1 (.D(in_09__t1), .en(we_09__t1), .Q(out_09__t1), .clk(Clock));  // open: clr
  Register #(.width(32)) _10__t2 (.D(in_10__t2), .en(we_10__t2), .Q(out_10__t2), .clk(Clock));  // open: clr
  Register #(.width(32)) _11__t3 (.D(in_11__t3), .en(we_11__t3), .Q(out_11__t3), .clk(Clock));  // open: clr
  Register #(.width(32)) _12__t4 (.D(in_12__t4), .en(we_12__t4), .Q(out_12__t4), .clk(Clock));  // open: clr
  Register #(.width(32)) _13__t5 (.D(in_13__t5), .en(we_13__t5), .Q(out_13__t5), .clk(Clock));  // open: clr
  Register #(.width(32)) _14__t6 (.D(in_14__t6), .en(we_14__t6), .Q(out_14__t6), .clk(Clock));  // open: clr
  Register #(.width(32)) _15__t7 (.D(in_15__t7), .en(we_15__t7), .Q(out_15__t7), .clk(Clock));  // open: clr
  Register #(.width(32)) _16__s0 (.D(in_16__s0), .en(we_16__s0), .Q(s0_Value), .clk(Clock));  // open: clr
  Register #(.width(32)) _17__s1 (.D(in_17__s1), .en(we_17__s1), .Q(s1_Value), .clk(Clock));  // open: clr
  Register #(.width(32)) _18__s2 (.D(in_18__s2), .en(we_18__s2), .Q(s2_Value), .clk(Clock));  // open: clr
  Register #(.width(32)) _19__s3 (.D(in_19__s3), .en(we_19__s3), .Q(out_19__s3), .clk(Clock));  // open: clr
  Register #(.width(32)) _20__s4 (.D(in_20__s4), .en(we_20__s4), .Q(out_20__s4), .clk(Clock));  // open: clr
  Register #(.width(32)) _21__s5 (.D(in_21__s5), .en(we_21__s5), .Q(out_21__s5), .clk(Clock));  // open: clr
  Register #(.width(32)) _22__s6 (.D(in_22__s6), .en(we_22__s6), .Q(out_22__s6), .clk(Clock));  // open: clr
  Register #(.width(32)) _23__s7 (.D(in_23__s7), .en(we_23__s7), .Q(out_23__s7), .clk(Clock));  // open: clr
  Multiplexer #(.select(5), .width(32)) multiplexer_2 (
    .in0({32{1'b0}}), .in1(out_01__at), .in2(out_02__v0), .in3(out_03__v1), .in4(out_04__a0),
    .in5(out_05__a1), .in6(out_06__a2), .in7(out_07__a3), .in8(out_08__vo), .in9(out_09__t1),
    .in10(out_10__t2), .in11(out_11__t3), .in12(out_12__t4), .in13(out_13__t5), .in14(out_14__t6),
    .in15(out_15__t7), .in16(s0_Value), .in17(s1_Value), .in18(s2_Value), .in19(out_19__s3),
    .in20(out_20__s4), .in21(out_21__s5), .in22(out_22__s6), .in23(out_23__s7), .in24(out_24__t8),
    .in25(out_25__t9), .in26(out_26__k0), .in27(out_27__k1), .in28(out_28__gp), .in29(sp_Value),
    .in30(out_30__fp), .in31(ra_Value), .out(Read_Data_2), .sel(Read_Register_2));  // open: en
  Register #(.width(32)) _24__t8 (.D(in_24__t8), .en(we_24__t8), .Q(out_24__t8), .clk(Clock));  // open: clr
  Register #(.width(32)) _25__t9 (.D(in_25__t9), .en(we_25__t9), .Q(out_25__t9), .clk(Clock));  // open: clr
  Register #(.width(32)) _26__k0 (.D(in_26__k0), .en(we_26__k0), .Q(out_26__k0), .clk(Clock));  // open: clr
  Register #(.width(32)) _27__k1 (.D(in_27__k1), .en(we_27__k1), .Q(out_27__k1), .clk(Clock));  // open: clr
  Register #(.width(32)) _28__gp (.D(in_28__gp), .en(we_28__gp), .Q(out_28__gp), .clk(Clock));  // open: clr
  Register #(.width(32)) _29__sp (.D(in_29__sp), .en(we_29__sp), .Q(sp_Value), .clk(Clock));  // open: clr
  Register #(.width(32)) _30__fp (.D(in_30__fp), .en(we_30__fp), .Q(out_30__fp), .clk(Clock));  // open: clr
  Register #(.width(32)) _31__ra (.D(in_31__ra), .en(we_31__ra), .Q(ra_Value), .clk(Clock));  // open: clr
  Demultiplexer #(.select(5), .width(32)) demultiplexer_2 (
    .out1(in_01__at), .out2(in_02__v0), .out3(in_03__v1), .out4(in_04__a0), .out5(in_05__a1),
    .out6(in_06__a2), .out7(in_07__a3), .out8(in_08__t0), .out9(in_09__t1), .out10(in_10__t2),
    .out11(in_11__t3), .out12(in_12__t4), .out13(in_13__t5), .out14(in_14__t6), .out15(in_15__t7),
    .out16(in_16__s0), .out17(in_17__s1), .out18(in_18__s2), .out19(in_19__s3), .out20(in_20__s4),
    .out21(in_21__s5), .out22(in_22__s6), .out23(in_23__s7), .out24(in_24__t8), .out25(in_25__t9),
    .out26(in_26__k0), .out27(in_27__k1), .out28(in_28__gp), .out29(in_29__sp), .out30(in_30__fp),
    .out31(in_31__ra), .in(Write_Data), .sel(Write_Register));  // open: out0, en

  // Other names for the same wires on the sheet: clk = Clock; out_16__s0[31:0] = s0_Value;
  //   out_17__s1[31:0] = s1_Value; out_18__s2[31:0] = s2_Value; out_29__sp[31:0] = sp_Value;
  //   out_31__ra[31:0] = ra_Value; read_data1[31:0] = Read_Data_1; read_data2[31:0] = Read_Data_2;
  //   read_reg1[4:0] = Read_Register_1; read_reg2[4:0] = Read_Register_2; write_en = Write_Enable;
  //   write_reg[4:0] = Write_Register

  // Notes on the sheet:
  //   INPUTS to your circuit
  //   DON'T CHANGE THE LOCATIONS OF THE INPUTS AND OUTPUTS!
  //   These are DEBUG/TEST outputs from your circuit.
  //   OUTPUTS from your circuit
endmodule
